// Digital circuit Gigatron_16bit_3.dig as structural Verilog
module Gigatron_16bit_3 (
  input  CLR,
  input  in_2,
  input  CLR_2,
  input  CK,
  input  in_5,
  input  CLK,
  input  HOLD_LD,
  input  CLR_3,
  input  nOE,
  input  in_10,
  input  CLR_4,
  input  in_12,
  input  CLR_5,
  input  in_14,
  input  in_15,
  input  in_16,
  input  in_17,
  input  in_18,
  input  in_19,
  input  in_20,
  input  in_21,
  input  in_22,
  input  in_23,
  input  in_24,
  input  in_25,
  input  in_26,
  input  CLK_2
);

  wire _74193_1_pin1, _74193_1_pin9, _74193_1_pin10, _74193_1_pin12, _74193_1_pin13, _74193_1_pin15,
       _74193_2_pin1, _74193_2_pin9, _74193_2_pin10, _74193_2_pin12, _74193_2_pin13, _74193_2_pin15,
       _74193_3_pin1, _74193_3_pin9, _74193_3_pin10, _74193_3_pin12, _74193_3_pin13, _74193_3_pin15,
       _74193_4_pin1, _74193_4_pin9, _74193_4_pin10, _74193_4_pin15, A0, A1, A2, A3, A4, A5, A6, A7, A8, A9,
       A10, A11, A12, A13, A14, A15, AC0, AC1, AC2, AC3, AC4, AC5, AC6, AC7, AC8, AC9, AC10, AC11, AC12,
       AC13, AC14, AC15, ADD, AL, ALU0, ALU1, ALU2, ALU3, ALU4, ALU5, ALU6, ALU7, ALU8, ALU9, ALU10, ALU11,
       ALU12, ALU13, ALU14, ALU15, AND, and_2_out, and_3_out, and_4_out, AR0, AR1, AR2, AR3, BUS0, BUS1,
       BUS2, BUS3, BUS4, BUS5, BUS6, BUS7, BUS8, BUS9, BUS10, BUS11, BUS12, BUS13, BUS14, BUS15, C_0, C_1,
       C_2, C_3, CLK2, CO, D0, D1, D2, D3, D4, D5, D6, D7, diodebackward_1_out, diodebackward_5_out,
       diodebackward_7_out, diodebackward_9_out, diodebackward_27_out, EH, EL, IC1_pin11, IC1_pin12,
       IC1_pin13, IC1_pin14, IC2_pin7, IC2_pin9, IC2_pin10, IC2_pin11, IC2_pin12, IC2_pin13, IC2_pin14,
       IC2_pin15, IC5_pin2, IC5_pin3, IC5_pin8, IC5_pin11, IC6_pin2, IC6_pin3, IC6_pin8, IC6_pin11, IC7_pin2,
       IC7_pin3, IC7_pin8, IC7_pin11, IC8_pin1, IC8_pin2, IC8_pin3, IC8_pin8, IC8_pin11, IC16_pin1,
       IC21_pin11, IC21_pin12, IC21_pin13, IC21_pin14, IC21_pin15, IC21_pin16, IC21_pin17, IC21_pin18, IR0,
       IR1, IR2, IR3, IR4, IR5, IR6, IR7, IX, LD, nAE, nBF, nDE, nIE, nJMP, nLD, nOE_t, nOL, not_1_out,
       not_2_out, not_3_out, not_4_out, not_5_out, not_6_out, not_7_out, not_9_out, nPH, nPL, nWE, nXL, nYL,
       OR, or_1_out, OUT0, OUT1, OUT2, OUT3, OUT4, OUT5, OUT6, OUT7, PC0, PC1, PC2, PC3, PC4, PC5, PC6, PC7,
       PC8, PC9, PC10, PC11, PC12, PC13, PC14, PC15, pullup_1_out, pullup_7_out, pullup_9_out, R0, R1, R2,
       R3, reset_1_out, SLOT, ST, SUB, SW0, SW1, SW2, SW3, SW4, SW5, SW6, SW7, U3_pin15, U4_pin15, U5_pin15,
       U7_p9, U7_p10, U7_p11, U7_p12, U7_p13, U7_p15, U7_p16, U7_p17, U7_p18, U7_p19, U7_p20, U7_p21, U7_p22,
       U8_pin2, U8_pin3, U8_pin4, U12_pin7, U13_pin7, U13_pin9, U13_pin12, U13_pin13, U13_pin14, U13_pin15,
       U17_pin7, U17_pin9, U18_pin7, U18_pin9, U19_pin7, U19_pin9, U20_pin7, U20_pin9, U21_pin7, U21_pin9,
       U22_pin7, U22_pin9, U23_pin7, U23_pin9, U24_pin7, U24_pin9, U25_2_pin7, U25_2_pin9, U26_2_pin7,
       U26_2_pin9, U27_pin7, U27_pin9, U28_pin7, U28_pin9, U29_2_pin7, U29_2_pin9, U29_pin15, U30_2_pin7,
       U30_2_pin9, U31_pin7, U31_pin9, U32_2_pin7, U32_2_pin9, U35_pin15, X0, X1, X2, X3, X4, X5, X6, X7,
       XOR, XOUT0, XOUT1, XOUT2, XOUT3, XOUT4, XOUT5, XOUT6, XOUT7, Y0, Y1, Y2, Y3, Y4, Y5, Y6, Y7;
  wire [3:0] _74193_1_pin3, _74193_2_pin3, _74193_3_pin3, _74193_4_pin3;

  // _62256 U36L: pin names not known; wires that end beside it: A14, A12, A7, A6, A5, A4, A3, A2, A1, A0, BUS0, BUS1, BUS2, 1'b0, 1'b1, nWE, A13, A8, A9, A11, nOE_t, A10, 1'b0, BUS7
  _74157 U33 (
    .pin1(1'b0), .pin2(Y4), .pin3(1'b1), .pin4(A12), .pin5(Y5), .pin6(1'b1), .pin7(A13), .pin8(1'b0),
    .pin9(A14), .pin10(1'b1), .pin11(Y6), .pin12(A15), .pin13(1'b1), .pin14(Y7), .pin15(EH), .pin16(1'b1));
  _74157 U32 (
    .pin1(1'b0), .pin2(Y0), .pin3(1'b1), .pin4(A8), .pin5(Y1), .pin6(1'b1), .pin7(A9), .pin8(1'b0),
    .pin9(A10), .pin10(1'b1), .pin11(Y2), .pin12(A11), .pin13(1'b1), .pin14(Y3), .pin15(EH), .pin16(1'b1));
  _74163 U29 (
    .pin1(1'b1), .pin2(CLK2), .pin3(ALU0), .pin4(ALU1), .pin5(ALU2), .pin6(ALU3), .pin7(IX), .pin8(1'b0),
    .pin9(nXL), .pin10(1'b1), .pin11(X3), .pin12(X2), .pin13(X1), .pin14(X0), .pin15(U29_pin15), .pin16(1'b1));
  _74163 U30 (
    .pin1(1'b1), .pin2(CLK2), .pin3(ALU4), .pin4(ALU5), .pin5(ALU6), .pin6(ALU7), .pin7(IX), .pin8(1'b0),
    .pin9(nXL), .pin10(U29_pin15), .pin11(X7), .pin12(X6), .pin13(X5), .pin14(X4), .pin16(1'b1));  // open: pin15
  _74157 U35 (
    .pin1(EL), .pin2(X4), .pin3(D4), .pin4(A4), .pin5(X5), .pin6(D5), .pin7(A5), .pin8(1'b0), .pin9(A6),
    .pin10(D6), .pin11(X6), .pin12(A7), .pin13(D7), .pin14(X7), .pin15(U35_pin15), .pin16(1'b1));
  _74157 U34 (
    .pin1(EL), .pin2(X0), .pin3(D0), .pin4(A0), .pin5(X1), .pin6(D1), .pin7(A1), .pin8(1'b0), .pin9(A2),
    .pin10(D2), .pin11(X2), .pin12(A3), .pin13(D3), .pin14(X3), .pin15(U35_pin15), .pin16(1'b1));
  and and_1 (U35_pin15, nWE, nOE_t);
  Seven_Seg_Hex seven_seg_hex_1 (.d({Y7, Y6, Y5, Y4}), .dp(1'b0));
  // _62256 U36H: pin names not known; wires that end beside it: A14, A12, A7, A6, A5, A4, A3, A2, A1, A0, BUS8, BUS9, BUS10, 1'b0, 1'b1, nWE, A13, A8, A9, A11, nOE_t, A10, 1'b0, BUS15
  Seven_Seg_Hex seven_seg_hex_2 (.d({Y3, Y2, Y1, Y0}), .dp(1'b0));
  Seven_Seg_Hex seven_seg_hex_3 (.d({X7, X6, X5, X4}), .dp(1'b0));
  not not_1 (not_1_out, nDE);
  not not_2 (not_2_out, nOE_t);
  not not_3 (not_3_out, nAE);
  not not_4 (not_4_out, nIE);
  not not_5 (not_5_out, nOL);
  _74540 IC21 (
    .pin1(1'b0), .pin2(LD), .pin3(AND), .pin4(OR), .pin5(XOR), .pin6(ADD), .pin7(SUB), .pin8(ST),
    .pin9(nJMP), .pin10(1'b0), .pin11(IC21_pin11), .pin12(IC21_pin12), .pin13(IC21_pin13),
    .pin14(IC21_pin14), .pin15(IC21_pin15), .pin16(IC21_pin16), .pin17(IC21_pin17), .pin18(IC21_pin18),
    .pin19(1'b0), .pin20(1'b1));
  LED led_1 (.in(XOUT3));
  LED led_2 (.in(XOUT2));
  _74173 U31A (
    .pin1(1'b0), .pin2(1'b0), .pin3(Y3), .pin4(Y2), .pin5(Y1), .pin6(Y0), .pin7(CLK2), .pin8(1'b0),
    .pin9(nYL), .pin10(nYL), .pin11(ALU0), .pin12(ALU1), .pin13(ALU2), .pin14(ALU3), .pin15(1'b0),
    .pin16(1'b1));
  _74173 U31B (
    .pin1(1'b0), .pin2(1'b0), .pin3(Y7), .pin4(Y6), .pin5(Y5), .pin6(Y4), .pin7(CLK2), .pin8(1'b0),
    .pin9(nYL), .pin10(nYL), .pin11(ALU4), .pin12(ALU5), .pin13(ALU6), .pin14(ALU7), .pin15(1'b0),
    .pin16(1'b1));
  Seven_Seg_Hex seven_seg_hex_4 (.d({X3, X2, X1, X0}), .dp(1'b0));
  LED DATA (.in(not_1_out));
  LED RAM (.in(not_2_out));
  LED ACC (.in(not_3_out));
  LED INPUT (.in(not_4_out));
  LED OUTPUT (.in(not_5_out));
  LED led_3 (.in(XOUT1));
  LED led_4 (.in(XOUT0));
  Seven_Seg_Hex seven_seg_hex_5 (.d({AC15, AC14, AC13, AC12}), .dp(1'b0));
  LED led_5 (.in(IC21_pin18));
  LED led_6 (.in(IC21_pin17));
  LED led_7 (.in(IC21_pin16));
  LED led_8 (.in(IC21_pin15));
  LED led_9 (.in(IC21_pin14));
  LED led_10 (.in(IC21_pin13));
  LED led_11 (.in(IC21_pin12));
  LED led_12 (.in(IC21_pin11));
  Delay delay_1 (.in(CLK), .out(CLK2));
  Seven_Seg_Hex seven_seg_hex_6 (.d({AC11, AC10, AC9, AC8}), .dp(1'b0));
  Reset reset_1 (.out(reset_1_out));
  Seven_Seg_Hex seven_seg_hex_7 (.d({AC7, AC6, AC5, AC4}), .dp(1'b0));
  _74163 U3 (
    .pin1(reset_1_out), .pin2(CLK), .pin3(BUS0), .pin4(BUS1), .pin5(BUS2), .pin6(BUS3), .pin7(1'b1),
    .pin8(1'b0), .pin9(nPL), .pin10(1'b1), .pin11(PC3), .pin12(PC2), .pin13(PC1), .pin14(PC0),
    .pin15(U3_pin15), .pin16(1'b1));
  _74163 U4 (
    .pin1(reset_1_out), .pin2(CLK), .pin3(BUS4), .pin4(BUS5), .pin5(BUS6), .pin6(BUS7), .pin7(1'b1),
    .pin8(1'b0), .pin9(nPL), .pin10(U3_pin15), .pin11(PC7), .pin12(PC6), .pin13(PC5), .pin14(PC4),
    .pin15(U4_pin15), .pin16(1'b1));
  _74163 U5 (
    .pin1(reset_1_out), .pin2(CLK), .pin3(Y0), .pin4(Y1), .pin5(Y2), .pin6(Y3), .pin7(1'b1), .pin8(1'b0),
    .pin9(nPH), .pin10(U4_pin15), .pin11(PC11), .pin12(PC10), .pin13(PC9), .pin14(PC8), .pin15(U5_pin15),
    .pin16(1'b1));
  _74163 U6 (
    .pin1(reset_1_out), .pin2(CLK), .pin3(Y4), .pin4(Y5), .pin5(Y6), .pin6(Y7), .pin7(1'b1), .pin8(1'b0),
    .pin9(nPH), .pin10(U5_pin15), .pin11(PC15), .pin12(PC14), .pin13(PC13), .pin14(PC12), .pin16(1'b1));  // open: pin15
  Seven_Seg_Hex seven_seg_hex_8 (.d({AC3, AC2, AC1, AC0}), .dp(1'b0));
  Seven_Seg_Hex seven_seg_hex_9 (.d({A15, A14, A13, A12}), .dp(1'b0));
  LED u_AL (.in(AL));
  LED u_AR0 (.in(AR0));
  LED u_AR1 (.in(AR1));
  LED u_AR2 (.in(AR2));
  LED u_AR3 (.in(AR3));
  LED u_nPH (.in(nPH));
  LED u_nPL (.in(nPL));
  LED u_EL (.in(EL));
  LED u_EH (.in(EH));
  LED u_nYL (.in(nYL));
  LED u_nXL (.in(nXL));
  LED u_IX (.in(IX));
  LED u_nWE (.in(nWE));
  LED u_nOE (.in(nOE_t));
  LED nACC (.in(nLD));
  LED nOUT (.in(nOL));
  LED Cin (.in(AR0));
  LED Cout (.in(CO));
  LED u_AC7 (.in(AC7));
  Seven_Seg_Hex seven_seg_hex_10 (.d({A11, A10, A9, A8}), .dp(1'b0));
  Seven_Seg_Hex seven_seg_hex_11 (.d({A7, A6, A5, A4}), .dp(1'b0));
  Seven_Seg_Hex seven_seg_hex_12 (.d({A3, A2, A1, A0}), .dp(1'b0));
  Seven_Seg_Hex seven_seg_hex_13 (.d({OUT7, OUT6, OUT5, OUT4}), .dp(1'b0));
  _7474 IC8 (
    .pin1(IC8_pin1), .pin2(IC8_pin2), .pin3(IC8_pin3), .pin4(1'b1), .pin5(SW7), .pin6(IC8_pin2), .pin7(1'b0),
    .pin8(IC8_pin8), .pin9(SW6), .pin10(1'b1), .pin11(IC8_pin11), .pin12(IC8_pin8), .pin13(IC8_pin1),
    .pin14(1'b1));
  Seven_Seg_Hex seven_seg_hex_14 (.d({OUT3, OUT2, OUT1, OUT0}), .dp(1'b0));
  Button #(.activeLow("true")) CLEAR (.out(IC8_pin1));
  _74161 IC1 (
    .pin1(1'b1), .pin2(CLK_2), .pin3(in_23), .pin4(in_24), .pin5(in_25), .pin6(in_26), .pin7(1'b1),
    .pin8(1'b0), .pin9(1'b1), .pin10(1'b1), .pin11(IC1_pin11), .pin12(IC1_pin12), .pin13(IC1_pin13),
    .pin14(IC1_pin14), .pin16(1'b1));  // open: pin15
  Seven_Seg_Hex seven_seg_hex_15 (.d({BUS15, BUS14, BUS13, BUS12}), .dp(1'b0));
  Seven_Seg_Hex seven_seg_hex_16 (.d({BUS11, BUS10, BUS9, BUS8}), .dp(1'b0));
  _7474 IC7 (
    .pin1(IC8_pin1), .pin2(IC7_pin2), .pin3(IC7_pin3), .pin4(1'b1), .pin5(SW4), .pin6(IC7_pin2), .pin7(1'b0),
    .pin8(IC7_pin8), .pin9(SW5), .pin10(1'b1), .pin11(IC7_pin11), .pin12(IC7_pin8), .pin13(IC8_pin1),
    .pin14(1'b1));
  LED led_13 (.in(SW7));
  Button button_1 (.out(IC8_pin3));
  Seven_Seg_Hex seven_seg_hex_17 (.d({BUS7, BUS6, BUS5, BUS4}), .dp(1'b0));
  LED led_14 (.in(SW6));
  Button button_2 (.out(IC8_pin11));
  // _27C1024 U7: pin names not known; wires that end beside it: PC9, PC10, PC11, PC12, PC13, PC14, PC15, 1'b1, U7_p9, U7_p10, U7_p11, U7_p12, U7_p13, 1'b0, U7_p15, U7_p16, U7_p17, U7_p18, U7_p19, U7_p20, U7_p21, U7_p22, 1'b0, 1'b1
  Seven_Seg_Hex seven_seg_hex_18 (.d({BUS3, BUS2, BUS1, BUS0}), .dp(1'b0));
  _74138 IC2 (
    .pin1(IC1_pin14), .pin2(IC1_pin13), .pin3(IC1_pin12), .pin4(1'b0), .pin5(1'b0), .pin6(CLK_2),
    .pin7(IC2_pin7), .pin8(1'b0), .pin9(IC2_pin9), .pin10(IC2_pin10), .pin11(IC2_pin11), .pin12(IC2_pin12),
    .pin13(IC2_pin13), .pin14(IC2_pin14), .pin15(IC2_pin15), .pin16(1'b1));
  _74574 U10 (
    .pin1(1'b0), .pin2(SW0), .pin3(SW1), .pin4(SW2), .pin5(SW3), .pin6(SW4), .pin7(SW5), .pin8(SW6),
    .pin9(SW7), .pin10(1'b0), .pin11(CLK), .pin12(IR7), .pin13(IR6), .pin14(IR5), .pin15(IR4), .pin16(IR3),
    .pin17(IR2), .pin18(IR1), .pin19(IR0), .pin20(1'b1));
  LED led_15 (.in(SW5));
  Button button_3 (.out(IC7_pin11));
  PullUp pullup_1 (.out(pullup_1_out));
  Seven_Seg_Hex seven_seg_hex_19 (.d({PC15, PC14, PC13, PC12}), .dp(1'b0));
  LED led_16 (.in(SW4));
  Button button_4 (.out(IC7_pin3));
  _74574 U8 (
    .pin1(pullup_1_out), .pin2(U8_pin2), .pin3(U8_pin3), .pin4(U8_pin4), .pin5(U7_p9), .pin6(U7_p10),
    .pin7(U7_p11), .pin8(U7_p12), .pin9(U7_p13), .pin10(1'b0), .pin11(1'b0), .pin12(IR7), .pin13(IR6),
    .pin14(IR5), .pin15(IR4), .pin16(IR3), .pin17(IR2), .pin18(IR1), .pin19(IR0), .pin20(1'b1));
  _74574 U9 (
    .pin1(1'b0), .pin2(U7_p15), .pin3(U7_p16), .pin4(U7_p17), .pin5(U7_p18), .pin6(U7_p19), .pin7(U7_p20),
    .pin8(U7_p21), .pin9(U7_p22), .pin10(1'b0), .pin11(1'b0), .pin12(D7), .pin13(D6), .pin14(D5), .pin15(D4),
    .pin16(D3), .pin17(D2), .pin18(D1), .pin19(D0), .pin20(1'b1));
  Seven_Seg_Hex seven_seg_hex_20 (.d({PC11, PC10, PC9, PC8}), .dp(1'b0));
  _7474 IC6 (
    .pin1(IC8_pin1), .pin2(IC6_pin2), .pin3(IC6_pin3), .pin4(1'b1), .pin5(SW3), .pin6(IC6_pin2), .pin7(1'b0),
    .pin8(IC6_pin8), .pin9(SW2), .pin10(1'b1), .pin11(IC6_pin11), .pin12(IC6_pin8), .pin13(IC8_pin1),
    .pin14(1'b1));
  Seven_Seg_Hex seven_seg_hex_21 (.d({PC7, PC6, PC5, PC4}), .dp(1'b0));
  LED led_17 (.in(SW3));
  Button button_5 (.out(IC6_pin3));
  Seven_Seg_Hex seven_seg_hex_22 (.d({PC3, PC2, PC1, PC0}), .dp(1'b0));
  LED led_18 (.in(SW2));
  Button button_6 (.out(IC6_pin11));
  // Probe T0 on IC2_pin15
  // Probe T1 on IC2_pin14
  // Probe T2 on IC2_pin13
  // Probe T3 on IC2_pin12
  // Probe T4 on IC2_pin11
  // Probe T5 on IC2_pin10
  // Probe T6 on IC2_pin9
  // Probe T7 on IC2_pin7
  Seven_Seg_Hex seven_seg_hex_23 (.d({IR7, IR6, IR5, IR4}), .dp(1'b0));
  LED led_19 (.in(SW1));
  _7474 IC5 (
    .pin1(IC8_pin1), .pin2(IC5_pin2), .pin3(IC5_pin3), .pin4(1'b1), .pin5(SW0), .pin6(IC5_pin2), .pin7(1'b0),
    .pin8(IC5_pin8), .pin9(SW1), .pin10(1'b1), .pin11(IC5_pin11), .pin12(IC5_pin8), .pin13(IC8_pin1),
    .pin14(1'b1));
  Button button_7 (.out(IC5_pin11));
  LED led_20 (.in(IC2_pin15));
  LED led_21 (.in(IC2_pin14));
  LED led_22 (.in(IC2_pin13));
  LED led_23 (.in(IC2_pin12));
  LED led_24 (.in(IC2_pin11));
  LED led_25 (.in(IC2_pin10));
  LED led_26 (.in(IC2_pin9));
  LED led_27 (.in(IC2_pin7));
  Seven_Seg_Hex seven_seg_hex_24 (.d({IR3, IR2, IR1, IR0}), .dp(1'b0));
  LED led_28 (.in(SW0));
  Button button_8 (.out(IC5_pin3));
  _74157 U36 (
    .pin1(SLOT), .pin2(1'b0), .pin3(IR0), .pin4(R0), .pin5(1'b0), .pin6(IR1), .pin7(R1), .pin8(1'b0),
    .pin9(R2), .pin10(IR2), .pin11(1'b0), .pin12(R3), .pin13(IR3), .pin14(1'b0), .pin15(1'b0), .pin16(1'b1));
  Seven_Seg_Hex seven_seg_hex_25 (.d({SW7, SW6, SW5, SW4}), .dp(1'b0));
  _74541 U10_2 (
    .pin1(nDE), .pin2(D0), .pin3(D1), .pin4(D2), .pin5(D3), .pin6(D4), .pin7(D5), .pin8(D6), .pin9(D7),
    .pin10(1'b0), .pin11(BUS7), .pin12(BUS6), .pin13(BUS5), .pin14(BUS4), .pin15(BUS3), .pin16(BUS2),
    .pin17(BUS1), .pin18(BUS0), .pin19(nDE), .pin20(1'b1));
  Seven_Seg_Hex seven_seg_hex_26 (.d({SW3, SW2, SW1, SW0}), .dp(1'b0));
  Seven_Seg_Hex seven_seg_hex_27 (.d({D7, D6, D5, D4}), .dp(1'b0));
  Seven_Seg_Hex seven_seg_hex_28 (.d({D3, D2, D1, D0}), .dp(1'b0));
  _74139 U11 (
    .pin1(1'b0), .pin2(IR0), .pin3(IR1), .pin4(nDE), .pin5(nOE_t), .pin6(nAE), .pin7(nIE), .pin8(1'b0),
    .pin12(nBF), .pin13(IR2), .pin14(IR3), .pin15(IR4), .pin16(1'b1));  // open: pin9, pin10, pin11
  _74138 U13 (
    .pin1(IR2), .pin2(IR3), .pin3(IR4), .pin4(1'b0), .pin5(1'b0), .pin6(nJMP), .pin7(U13_pin7), .pin8(1'b0),
    .pin9(U13_pin9), .pin10(nYL), .pin11(nXL), .pin12(U13_pin12), .pin13(U13_pin13), .pin14(U13_pin14),
    .pin15(U13_pin15), .pin16(1'b1));
  _74138 U14 (
    .pin1(IR5), .pin2(IR6), .pin3(IR7), .pin4(1'b0), .pin5(1'b0), .pin6(1'b1), .pin7(nJMP), .pin8(1'b0),
    .pin9(ST), .pin10(SUB), .pin11(ADD), .pin12(XOR), .pin13(OR), .pin14(AND), .pin15(LD), .pin16(1'b1));
  or or_1 (or_1_out, IR3, IR2);
  not not_6 (not_6_out, IR4);
  _74173 U37B (
    .pin1(1'b0), .pin2(1'b0), .pin3(OUT7), .pin4(OUT6), .pin5(OUT5), .pin6(OUT4), .pin7(CLK2), .pin8(1'b0),
    .pin9(nOL), .pin10(nOL), .pin11(ALU4), .pin12(ALU5), .pin13(ALU6), .pin14(ALU7), .pin15(1'b0),
    .pin16(1'b1));
  _74173 U37A (
    .pin1(1'b0), .pin2(1'b0), .pin3(OUT3), .pin4(OUT2), .pin5(OUT1), .pin6(OUT0), .pin7(CLK2), .pin8(1'b0),
    .pin9(nOL), .pin10(nOL), .pin11(ALU0), .pin12(ALU1), .pin13(ALU2), .pin14(ALU3), .pin15(1'b0),
    .pin16(1'b1));
  _74541 U28L (
    .pin1(nAE), .pin2(AC7), .pin3(AC6), .pin4(AC5), .pin5(AC4), .pin6(AC3), .pin7(AC2), .pin8(AC1),
    .pin9(AC0), .pin10(1'b0), .pin11(BUS0), .pin12(BUS1), .pin13(BUS2), .pin14(BUS3), .pin15(BUS4),
    .pin16(BUS5), .pin17(BUS6), .pin18(BUS7), .pin19(nAE), .pin20(1'b1));
  and and_2 (and_2_out, ST, nJMP);
  and and_3 (and_3_out, or_1_out, not_6_out);
  DiodeBackward diodebackward_1 (.in(U13_pin15), .out(diodebackward_1_out));
  DiodeBackward diodebackward_2 (.in(U13_pin14), .out(diodebackward_1_out));
  DiodeBackward diodebackward_3 (.in(U13_pin13), .out(diodebackward_1_out));
  DiodeBackward diodebackward_4 (.in(U13_pin12), .out(diodebackward_1_out));
  DiodeBackward diodebackward_5 (.in(IR7), .out(diodebackward_5_out));
  DiodeBackward diodebackward_6 (.in(nJMP), .out(diodebackward_5_out));
  PullUp pullup_2 (.out(diodebackward_1_out));
  DiodeBackward diodebackward_7 (.in(U13_pin9), .out(diodebackward_7_out));
  DiodeBackward diodebackward_8 (.in(U13_pin7), .out(diodebackward_7_out));
  PullUp pullup_3 (.out(diodebackward_5_out));
  DiodeBackward diodebackward_9 (.in(LD), .out(diodebackward_9_out));
  DiodeBackward diodebackward_10 (.in(AND), .out(diodebackward_9_out));
  DiodeBackward diodebackward_11 (.in(OR), .out(diodebackward_9_out));
  DiodeBackward diodebackward_12 (.in(ADD), .out(diodebackward_9_out));
  and and_4 (and_4_out, nOE_t, and_3_out);
  PullUp pullup_4 (.out(diodebackward_7_out));
  PullUp pullup_5 (.out(EL));
  DiodeBackward diodebackward_13 (.in(U13_pin14), .out(EL));
  DiodeBackward diodebackward_14 (.in(U13_pin12), .out(EL));
  DiodeBackward diodebackward_15 (.in(U13_pin7), .out(EL));
  PullUp pullup_6 (.out(diodebackward_9_out));
  PullUp pullup_7 (.out(pullup_7_out));
  DiodeBackward diodebackward_16 (.in(LD), .out(pullup_7_out));
  DiodeBackward diodebackward_17 (.in(OR), .out(pullup_7_out));
  DiodeBackward diodebackward_18 (.in(XOR), .out(pullup_7_out));
  DiodeBackward diodebackward_19 (.in(ADD), .out(pullup_7_out));
  DiodeBackward diodebackward_20 (.in(ST), .out(pullup_7_out));
  PullUp pullup_8 (.out(EH));
  DiodeBackward diodebackward_21 (.in(U13_pin13), .out(EH));
  DiodeBackward diodebackward_22 (.in(U13_pin12), .out(EH));
  DiodeBackward diodebackward_23 (.in(U13_pin7), .out(EH));
  PullUp pullup_9 (.out(pullup_9_out));
  DiodeBackward diodebackward_24 (.in(OR), .out(pullup_9_out));
  DiodeBackward diodebackward_25 (.in(XOR), .out(pullup_9_out));
  DiodeBackward diodebackward_26 (.in(SUB), .out(pullup_9_out));
  DiodeBackward diodebackward_27 (.in(SUB), .out(diodebackward_27_out));
  DiodeBackward diodebackward_28 (.in(ST), .out(diodebackward_27_out));
  and and_5 (SLOT, and_2_out, and_4_out);
  _74541 U28H (
    .pin1(nAE), .pin2(AC15), .pin3(AC14), .pin4(AC13), .pin5(AC12), .pin6(AC11), .pin7(AC10), .pin8(AC9),
    .pin9(AC8), .pin10(1'b0), .pin11(BUS8), .pin12(BUS9), .pin13(BUS10), .pin14(BUS11), .pin15(BUS12),
    .pin16(BUS13), .pin17(BUS14), .pin18(BUS15), .pin19(nAE), .pin20(1'b1));
  PullUp pullup_10 (.out(CO));
  PullUp pullup_11 (.out(diodebackward_27_out));
  LED led_29 (.in(SLOT));
  _74153 U12 (
    .pin1(nJMP), .pin2(C_1), .pin3(1'b0), .pin4(IR4), .pin5(IR3), .pin6(IR2), .pin7(U12_pin7), .pin8(1'b0),
    .pin10(1'b1), .pin11(1'b1), .pin12(1'b1), .pin13(1'b1), .pin14(AC7), .pin15(1'b1), .pin16(1'b1));  // open: pin9
  not not_7 (not_7_out, U12_pin7);
  not not_8 (IX, U13_pin7);
  not not_9 (not_9_out, ST);
  _74173 IC16 (
    .pin1(IC16_pin1), .pin2(IC16_pin1), .pin3(BUS4), .pin4(BUS5), .pin5(BUS6), .pin6(BUS7), .pin7(CK),
    .pin8(1'b0), .pin9(HOLD_LD), .pin10(HOLD_LD), .pin11(SW7), .pin12(SW6), .pin13(SW5), .pin14(SW4),
    .pin15(CLR_3), .pin16(1'b1));
  _74173 IC15 (
    .pin1(IC16_pin1), .pin2(IC16_pin1), .pin3(BUS0), .pin4(BUS1), .pin5(BUS2), .pin6(BUS3), .pin7(CK),
    .pin8(1'b0), .pin9(HOLD_LD), .pin10(HOLD_LD), .pin11(SW3), .pin12(SW2), .pin13(SW1), .pin14(SW0),
    .pin15(CLR_3), .pin16(1'b1));
  DiodeBackward diodebackward_29 (.in(not_7_out), .out(nPL));
  DiodeBackward diodebackward_30 (.in(nPH), .out(nPL));
  or or_2 (nOL, diodebackward_7_out, not_9_out);
  or or_3 (nLD, diodebackward_1_out, not_9_out);
  or or_4 (nWE, CLK, ST);
  or or_5 (nPH, nBF, nJMP);
  _74540 U15 (
    .pin1(1'b0), .pin2(diodebackward_9_out), .pin3(pullup_7_out), .pin4(pullup_9_out),
    .pin5(diodebackward_27_out), .pin6(diodebackward_5_out), .pin7(1'b0), .pin8(1'b0), .pin9(1'b0),
    .pin10(1'b0), .pin14(AL), .pin15(AR0), .pin16(AR1), .pin17(AR2), .pin18(AR3), .pin19(1'b0), .pin20(1'b1));  // open: pin11, pin12, pin13
  _74573 U38 (
    .pin1(in_5), .pin2(AC7), .pin3(AC6), .pin4(AC5), .pin5(AC4), .pin6(AC3), .pin7(AC2), .pin8(AC1),
    .pin9(AC0), .pin10(1'b0), .pin11(OUT6), .pin12(XOUT0), .pin13(XOUT1), .pin14(XOUT2), .pin15(XOUT3),
    .pin16(XOUT4), .pin17(XOUT5), .pin18(XOUT6), .pin19(XOUT7), .pin20(1'b1));
  PullUp pullup_12 (.out(nPL));
  not not_10 (IC16_pin1, nOE);
  _74153 U20 (
    .pin1(1'b0), .pin2(BUS7), .pin3(AR3), .pin4(AR2), .pin5(AR1), .pin6(AR0), .pin7(U20_pin7), .pin8(1'b0),
    .pin9(U20_pin9), .pin10(1'b0), .pin11(1'b1), .pin12(1'b0), .pin13(1'b1), .pin14(AC7), .pin15(AL),
    .pin16(1'b1));
  _74153 U19 (
    .pin1(1'b0), .pin2(BUS6), .pin3(AR3), .pin4(AR2), .pin5(AR1), .pin6(AR0), .pin7(U19_pin7), .pin8(1'b0),
    .pin9(U19_pin9), .pin10(1'b0), .pin11(1'b1), .pin12(1'b0), .pin13(1'b1), .pin14(AC6), .pin15(AL),
    .pin16(1'b1));
  _74153 U18 (
    .pin1(1'b0), .pin2(BUS5), .pin3(AR3), .pin4(AR2), .pin5(AR1), .pin6(AR0), .pin7(U18_pin7), .pin8(1'b0),
    .pin9(U18_pin9), .pin10(1'b0), .pin11(1'b1), .pin12(1'b0), .pin13(1'b1), .pin14(AC5), .pin15(AL),
    .pin16(1'b1));
  _74153 U17 (
    .pin1(1'b0), .pin2(BUS4), .pin3(AR3), .pin4(AR2), .pin5(AR1), .pin6(AR0), .pin7(U17_pin7), .pin8(1'b0),
    .pin9(U17_pin9), .pin10(1'b0), .pin11(1'b1), .pin12(1'b0), .pin13(1'b1), .pin14(AC4), .pin15(AL),
    .pin16(1'b1));
  _74153 U24 (
    .pin1(1'b0), .pin2(BUS3), .pin3(AR3), .pin4(AR2), .pin5(AR1), .pin6(AR0), .pin7(U24_pin7), .pin8(1'b0),
    .pin9(U24_pin9), .pin10(1'b0), .pin11(1'b1), .pin12(1'b0), .pin13(1'b1), .pin14(AC3), .pin15(AL),
    .pin16(1'b1));
  _74153 U23 (
    .pin1(1'b0), .pin2(BUS2), .pin3(AR3), .pin4(AR2), .pin5(AR1), .pin6(AR0), .pin7(U23_pin7), .pin8(1'b0),
    .pin9(U23_pin9), .pin10(1'b0), .pin11(1'b1), .pin12(1'b0), .pin13(1'b1), .pin14(AC2), .pin15(AL),
    .pin16(1'b1));
  _74153 U22 (
    .pin1(1'b0), .pin2(BUS1), .pin3(AR3), .pin4(AR2), .pin5(AR1), .pin6(AR0), .pin7(U22_pin7), .pin8(1'b0),
    .pin9(U22_pin9), .pin10(1'b0), .pin11(1'b1), .pin12(1'b0), .pin13(1'b1), .pin14(AC1), .pin15(AL),
    .pin16(1'b1));
  _74153 U21 (
    .pin1(1'b0), .pin2(BUS0), .pin3(AR3), .pin4(AR2), .pin5(AR1), .pin6(AR0), .pin7(U21_pin7), .pin8(1'b0),
    .pin9(U21_pin9), .pin10(1'b0), .pin11(1'b1), .pin12(1'b0), .pin13(1'b1), .pin14(AC0), .pin15(AL),
    .pin16(1'b1));
  _74283 U25 (
    .pin1(ALU5), .pin2(U18_pin9), .pin3(U18_pin7), .pin4(ALU4), .pin5(U17_pin7), .pin6(U17_pin9), .pin7(C_0),
    .pin8(1'b0), .pin9(C_1), .pin10(ALU7), .pin11(U20_pin9), .pin12(U20_pin7), .pin13(ALU6),
    .pin14(U19_pin7), .pin15(U19_pin9), .pin16(1'b1));
  _74283 U26 (
    .pin1(ALU1), .pin2(U22_pin9), .pin3(U22_pin7), .pin4(ALU0), .pin5(U21_pin7), .pin6(U21_pin9), .pin7(AR0),
    .pin8(1'b0), .pin9(C_0), .pin10(ALU3), .pin11(U24_pin9), .pin12(U24_pin7), .pin13(ALU2),
    .pin14(U23_pin7), .pin15(U23_pin9), .pin16(1'b1));
  LED led_30 (.in(C_1));
  _74173 U27B (
    .pin1(in_10), .pin2(in_10), .pin3(AC4), .pin4(AC5), .pin5(AC6), .pin6(AC7), .pin7(CLK2), .pin8(1'b0),
    .pin9(nLD), .pin10(nLD), .pin11(ALU7), .pin12(ALU6), .pin13(ALU5), .pin14(ALU4), .pin15(CLR_2),
    .pin16(1'b1));
  _74173 U27A (
    .pin1(in_2), .pin2(in_2), .pin3(AC0), .pin4(AC1), .pin5(AC2), .pin6(AC3), .pin7(CLK2), .pin8(1'b0),
    .pin9(nLD), .pin10(nLD), .pin11(ALU3), .pin12(ALU2), .pin13(ALU1), .pin14(ALU0), .pin15(CLR), .pin16(1'b1));
  _74153 U28 (
    .pin1(1'b0), .pin2(BUS15), .pin3(AR3), .pin4(AR2), .pin5(AR1), .pin6(AR0), .pin7(U28_pin7), .pin8(1'b0),
    .pin9(U28_pin9), .pin10(1'b0), .pin11(1'b1), .pin12(1'b0), .pin13(1'b1), .pin14(AC15), .pin15(AL),
    .pin16(1'b1));
  _74153 U27 (
    .pin1(1'b0), .pin2(BUS14), .pin3(AR3), .pin4(AR2), .pin5(AR1), .pin6(AR0), .pin7(U27_pin7), .pin8(1'b0),
    .pin9(U27_pin9), .pin10(1'b0), .pin11(1'b1), .pin12(1'b0), .pin13(1'b1), .pin14(AC14), .pin15(AL),
    .pin16(1'b1));
  _74153 U26_2 (
    .pin1(1'b0), .pin2(BUS13), .pin3(AR3), .pin4(AR2), .pin5(AR1), .pin6(AR0), .pin7(U26_2_pin7),
    .pin8(1'b0), .pin9(U26_2_pin9), .pin10(1'b0), .pin11(1'b1), .pin12(1'b0), .pin13(1'b1), .pin14(AC13),
    .pin15(AL), .pin16(1'b1));
  _74153 U25_2 (
    .pin1(1'b0), .pin2(BUS12), .pin3(AR3), .pin4(AR2), .pin5(AR1), .pin6(AR0), .pin7(U25_2_pin7),
    .pin8(1'b0), .pin9(U25_2_pin9), .pin10(1'b0), .pin11(1'b1), .pin12(1'b0), .pin13(1'b1), .pin14(AC12),
    .pin15(AL), .pin16(1'b1));
  _74153 U32_2 (
    .pin1(1'b0), .pin2(BUS11), .pin3(AR3), .pin4(AR2), .pin5(AR1), .pin6(AR0), .pin7(U32_2_pin7),
    .pin8(1'b0), .pin9(U32_2_pin9), .pin10(1'b0), .pin11(1'b1), .pin12(1'b0), .pin13(1'b1), .pin14(AC11),
    .pin15(AL), .pin16(1'b1));
  _74153 U31 (
    .pin1(1'b0), .pin2(BUS10), .pin3(AR3), .pin4(AR2), .pin5(AR1), .pin6(AR0), .pin7(U31_pin7), .pin8(1'b0),
    .pin9(U31_pin9), .pin10(1'b0), .pin11(1'b1), .pin12(1'b0), .pin13(1'b1), .pin14(AC10), .pin15(AL),
    .pin16(1'b1));
  _74153 U30_2 (
    .pin1(1'b0), .pin2(BUS9), .pin3(AR3), .pin4(AR2), .pin5(AR1), .pin6(AR0), .pin7(U30_2_pin7), .pin8(1'b0),
    .pin9(U30_2_pin9), .pin10(1'b0), .pin11(1'b1), .pin12(1'b0), .pin13(1'b1), .pin14(AC9), .pin15(AL),
    .pin16(1'b1));
  _74153 U29_2 (
    .pin1(1'b0), .pin2(BUS8), .pin3(AR3), .pin4(AR2), .pin5(AR1), .pin6(AR0), .pin7(U29_2_pin7), .pin8(1'b0),
    .pin9(U29_2_pin9), .pin10(1'b0), .pin11(1'b1), .pin12(1'b0), .pin13(1'b1), .pin14(AC8), .pin15(AL),
    .pin16(1'b1));
  _74283 U27_2 (
    .pin1(ALU13), .pin2(U26_2_pin9), .pin3(U26_2_pin7), .pin4(ALU12), .pin5(U25_2_pin7), .pin6(U25_2_pin9),
    .pin7(C_2), .pin8(1'b0), .pin9(C_3), .pin10(ALU15), .pin11(U28_pin9), .pin12(U28_pin7), .pin13(ALU14),
    .pin14(U27_pin7), .pin15(U27_pin9), .pin16(1'b1));
  _74283 U28_2 (
    .pin1(ALU9), .pin2(U30_2_pin9), .pin3(U30_2_pin7), .pin4(ALU8), .pin5(U29_2_pin7), .pin6(U29_2_pin9),
    .pin7(C_1), .pin8(1'b0), .pin9(C_2), .pin10(ALU11), .pin11(U32_2_pin9), .pin12(U32_2_pin7),
    .pin13(ALU10), .pin14(U31_pin7), .pin15(U31_pin9), .pin16(1'b1));
  LED led_31 (.in(C_3));
  _74173 U27B_2 (
    .pin1(in_14), .pin2(in_14), .pin3(AC12), .pin4(AC13), .pin5(AC14), .pin6(AC15), .pin7(CLK2), .pin8(1'b0),
    .pin9(nLD), .pin10(nLD), .pin11(ALU15), .pin12(ALU14), .pin13(ALU13), .pin14(ALU12), .pin15(CLR_5),
    .pin16(1'b1));
  _74173 U27A_2 (
    .pin1(in_12), .pin2(in_12), .pin3(AC8), .pin4(AC9), .pin5(AC10), .pin6(AC11), .pin7(CLK2), .pin8(1'b0),
    .pin9(nLD), .pin10(nLD), .pin11(ALU11), .pin12(ALU10), .pin13(ALU9), .pin14(ALU8), .pin15(CLR_4),
    .pin16(1'b1));
  PullUp pullup_13 (.out(R3));
  Seven_Seg_Hex seven_seg_hex_29 (.d(_74193_4_pin3), .dp(1'b0));
  PullUp pullup_14 (.out(R2));
  PullUp pullup_15 (.out(R1));
  Seven_Seg_Hex seven_seg_hex_30 (.d(_74193_3_pin3), .dp(1'b0));
  PullUp pullup_16 (.out(R0));
  Seven_Seg_Hex seven_seg_hex_31 (.d(_74193_2_pin3), .dp(1'b0));
  _74193 _74193_1 (
    .pin1(_74193_1_pin1), .pin2(_74193_1_pin3[1]), .pin3(_74193_1_pin3[0]), .pin4(in_15), .pin5(in_16),
    .pin6(_74193_1_pin3[2]), .pin7(_74193_1_pin3[3]), .pin8(1'b0), .pin9(_74193_1_pin9),
    .pin10(_74193_1_pin10), .pin11(in_17), .pin12(_74193_1_pin12), .pin13(_74193_1_pin13), .pin14(in_18),
    .pin15(_74193_1_pin15), .pin16(1'b1));
  Seven_Seg_Hex seven_seg_hex_32 (.d(_74193_1_pin3), .dp(1'b0));
  _74173 _74173_1 (
    .pin1(1'b0), .pin2(1'b0), .pin3(_74193_1_pin15), .pin4(_74193_1_pin1), .pin5(_74193_1_pin10),
    .pin6(_74193_1_pin9), .pin7(in_19), .pin8(1'b0), .pin9(1'b0), .pin10(1'b0), .pin11(BUS3), .pin12(BUS2),
    .pin13(BUS1), .pin14(BUS0), .pin15(1'b0), .pin16(1'b1));
  _74219 _74219_1 (
    .pin1(R0), .pin2(in_20), .pin3(in_21), .pin4(BUS0), .pin5(BUS0), .pin6(BUS1), .pin7(BUS1), .pin8(1'b0),
    .pin9(BUS2), .pin10(BUS2), .pin11(BUS3), .pin12(BUS3), .pin13(R3), .pin14(R2), .pin15(R1), .pin16(1'b1));
  _74193 _74193_2 (
    .pin1(_74193_2_pin1), .pin2(_74193_2_pin3[1]), .pin3(_74193_2_pin3[0]), .pin4(_74193_1_pin13),
    .pin5(_74193_1_pin12), .pin6(_74193_2_pin3[2]), .pin7(_74193_2_pin3[3]), .pin8(1'b0),
    .pin9(_74193_2_pin9), .pin10(_74193_2_pin10), .pin11(in_17), .pin12(_74193_2_pin12),
    .pin13(_74193_2_pin13), .pin14(in_18), .pin15(_74193_2_pin15), .pin16(1'b1));
  _74173 _74173_2 (
    .pin1(1'b0), .pin2(1'b0), .pin3(_74193_2_pin15), .pin4(_74193_2_pin1), .pin5(_74193_2_pin10),
    .pin6(_74193_2_pin9), .pin7(in_19), .pin8(1'b0), .pin9(1'b0), .pin10(1'b0), .pin11(BUS7), .pin12(BUS6),
    .pin13(BUS5), .pin14(BUS4), .pin15(1'b0), .pin16(1'b1));
  _74219 _74219_2 (
    .pin1(R0), .pin2(in_20), .pin3(in_21), .pin4(BUS4), .pin5(BUS4), .pin6(BUS5), .pin7(BUS5), .pin8(1'b0),
    .pin9(BUS6), .pin10(BUS6), .pin11(BUS7), .pin12(BUS7), .pin13(R3), .pin14(R2), .pin15(R1), .pin16(1'b1));
  _74193 _74193_3 (
    .pin1(_74193_3_pin1), .pin2(_74193_3_pin3[1]), .pin3(_74193_3_pin3[0]), .pin4(_74193_2_pin13),
    .pin5(_74193_2_pin12), .pin6(_74193_3_pin3[2]), .pin7(_74193_3_pin3[3]), .pin8(1'b0),
    .pin9(_74193_3_pin9), .pin10(_74193_3_pin10), .pin11(in_17), .pin12(_74193_3_pin12),
    .pin13(_74193_3_pin13), .pin14(in_18), .pin15(_74193_3_pin15), .pin16(1'b1));
  _74173 _74173_3 (
    .pin1(1'b0), .pin2(1'b0), .pin3(_74193_3_pin15), .pin4(_74193_3_pin1), .pin5(_74193_3_pin10),
    .pin6(_74193_3_pin9), .pin7(in_19), .pin8(1'b0), .pin9(1'b0), .pin10(1'b0), .pin11(BUS11), .pin12(BUS10),
    .pin13(BUS9), .pin14(BUS8), .pin15(1'b0), .pin16(1'b1));
  _74219 _74219_3 (
    .pin1(R0), .pin2(in_20), .pin3(in_21), .pin4(BUS8), .pin5(BUS8), .pin6(BUS9), .pin7(BUS9), .pin8(1'b0),
    .pin9(BUS10), .pin10(BUS10), .pin11(BUS11), .pin12(BUS11), .pin13(R3), .pin14(R2), .pin15(R1),
    .pin16(1'b1));
  _74193 _74193_4 (
    .pin1(_74193_4_pin1), .pin2(_74193_4_pin3[1]), .pin3(_74193_4_pin3[0]), .pin4(_74193_3_pin13),
    .pin5(_74193_3_pin12), .pin6(_74193_4_pin3[2]), .pin7(_74193_4_pin3[3]), .pin8(1'b0),
    .pin9(_74193_4_pin9), .pin10(_74193_4_pin10), .pin11(in_17), .pin14(in_18), .pin15(_74193_4_pin15),
    .pin16(1'b1));  // open: pin12, pin13
  _74173 _74173_4 (
    .pin1(1'b0), .pin2(1'b0), .pin3(_74193_4_pin15), .pin4(_74193_4_pin1), .pin5(_74193_4_pin10),
    .pin6(_74193_4_pin9), .pin7(in_19), .pin8(1'b0), .pin9(1'b0), .pin10(1'b0), .pin11(BUS15), .pin12(BUS14),
    .pin13(BUS13), .pin14(BUS12), .pin15(1'b0), .pin16(1'b1));
  _74541 _74541_1 (
    .pin1(in_22), .pin2(_74193_4_pin3[3]), .pin3(_74193_4_pin3[2]), .pin4(_74193_4_pin3[1]),
    .pin5(_74193_4_pin3[0]), .pin6(_74193_3_pin3[3]), .pin7(_74193_3_pin3[2]), .pin8(_74193_3_pin3[1]),
    .pin9(_74193_3_pin3[0]), .pin10(1'b0), .pin11(BUS8), .pin12(BUS9), .pin13(BUS10), .pin14(BUS11),
    .pin15(BUS12), .pin16(BUS13), .pin17(BUS14), .pin18(BUS15), .pin19(in_22), .pin20(1'b1));
  _74541 _74541_2 (
    .pin1(in_22), .pin2(_74193_2_pin3[3]), .pin3(_74193_2_pin3[2]), .pin4(_74193_2_pin3[1]),
    .pin5(_74193_2_pin3[0]), .pin6(_74193_1_pin3[3]), .pin7(_74193_1_pin3[2]), .pin8(_74193_1_pin3[1]),
    .pin9(_74193_1_pin3[0]), .pin10(1'b0), .pin11(BUS0), .pin12(BUS1), .pin13(BUS2), .pin14(BUS3),
    .pin15(BUS4), .pin16(BUS5), .pin17(BUS6), .pin18(BUS7), .pin19(in_22), .pin20(1'b1));
  _74219 _74219_4 (
    .pin1(R0), .pin2(in_20), .pin3(in_21), .pin4(BUS12), .pin5(BUS12), .pin6(BUS13), .pin7(BUS13),
    .pin8(1'b0), .pin9(BUS14), .pin10(BUS14), .pin11(BUS15), .pin12(BUS15), .pin13(R3), .pin14(R2),
    .pin15(R1), .pin16(1'b1));

  // Other names for the same wires on the sheet: CLK1 = CLK

  // Notes on the sheet:
  //   CLK: Hz: 1000
  //   RAM & X Y REGS
  //   X REGISTER
  //   Y SELECT
  //   X SELECT
  //   32K RAM
  //   PROGRAM COUNTER & ROM
  //   FRONT PANEL SWITCHES
  //   Y REG
  //   Y REGISTER
  //   BUS SOURCE
  //   INSTRUCTION
  //   XOUT LEDS
  //   X REG
  //   AC-HI
  //   LOAD
  //   AND
  //   OR
  //   XOR
  //   ADD
  //   SUB
  //   STORE
  //   JMP
  //   AC-LO
  //   CONTROL
  //   RAM ADDRESS
  //   OUTPUT
  //   Bit Counter
  //   BUS DATA
  //   Bit Slot Decoder
  //   PC ADDRESS
  //   Bit Slot
  //   SWITCHES
  //   DATA
  //   CONTROL UNIT
  //   REGISTERS
  //   16-bit Jump Detector
  //   OUTPUT REGISTER
  //   AC -> BUS
  //   SWITCH REGISTER
  //   U15
  //   EXT. OUTPUT
  //   U16
  //   ALU-1
  //   ALU-0
  //   MUX7
  //   MUX6
  //   MUX5
  //   MUX4
  //   MUX3
  //   MUX2
  //   MUX1
  //   MUX0
  //   ACCUMULATOR
  //   ADDER
  //   Cout
  //   ALU-3
  //   ALU-2
  //   ADDRESS
endmodule
